# Fritzing sketch DIPSY_RPi_modela (saved by Fritzing 0.9.2b)
breadboards: 1

parts:
  IC1 = IC, DIP package, 8 pins [chip_label=DIPSY]
  Raspberry_Pi1 = Raspberry Pi A

nets:
  N1: IC1.pin1, Raspberry_Pi1.GPIO_25
  N2: IC1.pin2, Raspberry_Pi1.GPIO_15
  N3: IC1.pin3, Raspberry_Pi1.GPIO_24
  N4: IC1.pin4, Raspberry_Pi1.GND
  N5: IC1.pin5, Raspberry_Pi1.GPIO_10
  N6: IC1.pin6, Raspberry_Pi1.GPIO_9
  N7: IC1.pin7, Raspberry_Pi1.GPIO_11
  N8: IC1.pin8, Raspberry_Pi1.3V3

notes:
  System On Chip, a small Field Programmable Device that can be configured by Raspberry Pi to implement different hardware functions. Minimal connections are displayed, DIPSY is configured and can be used as read-write SPI Peripheral
  Hackaday Best Product Price Finalist 2015
  HTTP://DIPSY.COOL
  https://hackaday.io/project/6592-dipsy
