# Fritzing sketch DIPSY_EDISON (saved by Fritzing 0.9.2b)
breadboards: 1

parts:
  IC1 = IC, DIP package, 8 pins [chip_label=DIPSY]
  U1 = Intel Edison Arduinobreakout

nets:
  N1: IC1.pin1, U1.D8
  N2: IC1.pin2, U1.D10_PWM/SS
  N3: IC1.pin3, U1.D9_PWM
  N4: IC1.pin4, U1.GND
  N5: IC1.pin5, U1.D11_PWM/MOSI
  N6: IC1.pin6, U1.D12/MISO
  N7: IC1.pin7, U1.D13/SCK
  N8: IC1.pin8, U1.3V3

notes:
  System On Chip, a small Field Programmable Device that can be configured by Edison to implement different hardware functions. Minimal connections are displayed, DIPSY is configured and can be used as read-write SPI Peripheral
  Hackaday Best Product Price Finalist 2015
  HTTP://DIPSY.COOL
  https://hackaday.io/project/6592-dipsy
  Jumper J9 to 2-3
  to select 3.3V IO Voltage!
