# Fritzing sketch DIPSY_Galileo (saved by Fritzing 0.9.2b)
breadboards: 1

parts:
  IC1 = IC, DIP package, 8 pins [chip_label=DIPSY]
  Part1 = Intel Galileo

nets:
  N1: IC1.pin4, Part1.GND
  N2: IC1.pin8, Part1.3V3

notes:
  System On Chip, a small Field Programmable Device that can be configured by Galileo to implement different hardware functions. Minimal connections are displayed, DIPSY is configured and can be used as read-write SPI Peripheral
  Hackaday Best Product Price Finalist 2015
  HTTP://DIPSY.COOL
  https://hackaday.io/project/6592-dipsy
