# Fritzing sketch DIPSY_Propeller (saved by Fritzing 0.9.2b)
breadboards: 1

parts:
  IC1 = IC, DIP package, 8 pins [chip_label=DIPSY]
  Propeller1 = Parallax Propeller D40 [package="DIP [THT]"]

nets:
  N1: IC1.pin1, Propeller1.P13
  N2: IC1.pin2, Propeller1.P14
  N3: IC1.pin3, Propeller1.P15
  N4: IC1.pin4, Propeller1.VSS
  N5: IC1.pin5, Propeller1.P18
  N6: IC1.pin6, Propeller1.P17
  N7: IC1.pin7, Propeller1.P16
  N8: IC1.pin8, Propeller1.VDD#31

notes:
  System On Chip, a small Field Programmable Device that can be configured by Parallax Propeller to implement different hardware functions. Minimal connections are displayed, DIPSY is configured and can be used as read-write SPI Peripheral
  Hackaday Best Product Price Finalist 2015
  HTTP://DIPSY.COOL
  https://hackaday.io/project/6592-dipsy
